// Logisim project Projeto.circ as structural Verilog
module MeioSomador (
  input  A,
  input  B,
  output out_3,
  output out_4
);

  xor xor_1 (out_3, B, A);
  and and_1 (out_4, A, B);
endmodule
